// Logisim project 4BitFlags.circ as structural Verilog: 1 circuit, main circuit main
module main (
  input  C___1,
  input  S___0,
  input  in_3,
  input  in_4,
  input  in_5,
  input  in_6,
  input  in_7,
  input  in_8,
  input  in_9,
  input  in_10,
  output C__Bit_4____1,
  output S__Bit3____0,
  output Z__Bit_2____1,
  output P__Bit_0____0
);

  wire Clock_out, nor_1_out, xor_1_out, xor_2_out, xor_3_out;

  Clock Clock (.out(Clock_out));
  xor xor_1 (xor_1_out, in_7, in_8);
  xor xor_2 (xor_2_out, xor_1_out, in_9);
  nor nor_1 (nor_1_out, in_3, in_4, in_5, in_6);
  xor xor_3 (xor_3_out, xor_2_out, in_10);
  D_Flip_Flop d_ff_1 (.clk(Clock_out), .D(C___1), .Q(C__Bit_4____1));  // open: Qn, preset, en, reset
  D_Flip_Flop d_ff_2 (.clk(Clock_out), .D(S___0), .Q(S__Bit3____0));  // open: Qn, preset, en, reset
  D_Flip_Flop d_ff_3 (.clk(Clock_out), .D(nor_1_out), .Q(Z__Bit_2____1));  // open: Qn, preset, en, reset
  D_Flip_Flop d_ff_4 (.clk(Clock_out), .D(xor_3_out), .Q(P__Bit_0____0));  // open: Qn, preset, en, reset
endmodule
