// Logisim project brijac4.circ as structural Verilog: 1 circuit, main circuit main
module main (
  input  in_1,
  output out_2,
  output out_3,
  output out_4
);

  wire and_1_out, clock_1_out, not_1_out;

  Clock clock_1 (.out(clock_1_out));
  J_K_Flip_Flop j_k_ff_1 (
    .J(in_1), .clk(clock_1_out), .K(in_1), .Q(out_3), .preset(in_1), .reset(not_1_out));  // open: Qn, en
  J_K_Flip_Flop j_k_ff_2 (
    .J(in_1), .clk(clock_1_out), .K(in_1), .Qn(out_4), .preset(in_1), .reset(not_1_out));  // open: Q, en
  J_K_Flip_Flop j_k_ff_3 (
    .J(in_1), .clk(clock_1_out), .K(in_1), .Q(out_2), .preset(in_1), .reset(not_1_out));  // open: Qn, en
  and and_1 (and_1_out, out_3, out_4, out_2);
  not not_1 (not_1_out, and_1_out);
endmodule
