// Logisim project brojac12.circ as structural Verilog: 1 circuit, main circuit main
module main (
  input  in_1
);

  wire and_1_out, and_2_out, clock_1_out;
  wire [3:0] t_ff_1_q;

  Clock clock_1 (.out(clock_1_out));
  T_Flip_Flop t_ff_1 (.clk(clock_1_out), .T(in_1), .Q(t_ff_1_q[0]));  // open: Qn, preset, reset, en
  and and_1 (and_1_out, t_ff_1_q[0], t_ff_1_q[1]);
  T_Flip_Flop t_ff_2 (.clk(clock_1_out), .T(t_ff_1_q[0]), .Q(t_ff_1_q[1]));  // open: Qn, preset, reset, en
  and and_2 (and_2_out, and_1_out, t_ff_1_q[2]);
  T_Flip_Flop t_ff_3 (.clk(clock_1_out), .T(and_1_out), .Q(t_ff_1_q[2]));  // open: Qn, preset, reset, en
  T_Flip_Flop t_ff_4 (.clk(clock_1_out), .T(and_2_out), .Q(t_ff_1_q[3]));  // open: Qn, preset, reset, en
  Hex_Digit_Display hex_digit_display_1 (.value(t_ff_1_q));  // open: dp
endmodule
