// Logisim project ff11.circ as structural Verilog: 1 circuit, main circuit main
module main (
  input  in_1,
  input  in_2,
  input  in_3,
  input  in_4,
  output out_5,
  output out_6
);

  wire clock_1_out, nand_1_out, nand_2_out, nand_3_out, nand_4_out;

  Clock clock_1 (.out(clock_1_out));
  nand nand_1 (nand_1_out, in_2, clock_1_out);
  nand nand_2 (nand_2_out, clock_1_out, in_3);
  nand nand_3 (nand_3_out, nand_1_out, out_6);
  nand nand_4 (nand_4_out, out_5, nand_2_out);
  and and_1 (out_5, in_1, nand_3_out);
  and and_2 (out_6, nand_4_out, in_4);
endmodule
