// Logisim project ff2.circ as structural Verilog: 1 circuit, main circuit main
module main (
  input  in_1,
  input  in_2,
  input  in_3,
  output out_4,
  output out_5,
  output out_6,
  output out_7
);

  wire and_1_out, nand_1_out, nand_2_out, not_1_out, not_2_out, not_3_out;

  not not_1 (not_1_out, in_2);
  and and_1 (and_1_out, not_1_out, in_2);
  nand nand_1 (nand_1_out, out_6, in_1, and_1_out);
  nand nand_2 (nand_2_out, and_1_out, in_3, out_5);
  not not_2 (not_2_out, nand_2_out);
  not not_3 (not_3_out, nand_1_out);
  S_R_Flip_Flop s_r_ff_1 (.S(not_3_out), .R(not_2_out), .Q(out_5), .Qn(out_6));  // open: clk, preset, reset, en

  assign out_4 = in_1;
  assign out_7 = in_3;
endmodule
