// Logisim project ff5.circ as structural Verilog: 1 circuit, main circuit main
module main (
  input  in_1,
  input  in_2,
  output out_3,
  output out_4,
  output out_5,
  output out_6
);

  wire nand_1_out, nand_2_out, not_1_out;

  not not_1 (not_1_out, in_1);
  nand nand_1 (nand_1_out, in_1, in_2);
  nand nand_2 (nand_2_out, in_2, not_1_out);
  nand nand_3 (out_4, nand_1_out, out_6);
  nand nand_4 (out_6, out_4, nand_2_out);

  assign out_3 = in_1;
  assign out_5 = in_2;
endmodule
