// Logisim project ff6.circ as structural Verilog: 1 circuit, main circuit main
module main (
  input  in_1,
  input  in_2,
  output out_3,
  output out_4
);

  wire and_1_out, and_2_out;

  and and_1 (and_1_out, out_4, in_1);
  and and_2 (and_2_out, in_2, out_3);
  S_R_Flip_Flop s_r_ff_1 (.S(and_1_out), .R(and_2_out), .Q(out_3), .Qn(out_4));  // open: clk, preset, reset, en
endmodule
