// Logisim project ff7.circ as structural Verilog: 1 circuit, main circuit main
module main (
  input  in_1,
  input  in_2,
  input  in_3,
  input  in_4,
  output out_5,
  output out_6
);

  wire clock_1_out, nand_1_out, nand_2_out;

  Clock clock_1 (.out(clock_1_out));
  not nand_1 (nand_1_out, in_2);  // NAND_Gate
  nand nand_2 (nand_2_out, clock_1_out, in_4);
  nand nand_3 (out_5, in_1, nand_1_out, out_6);
  nand nand_4 (out_6, out_5, nand_2_out, in_3);
endmodule
