// Logisim project taktiran SR.circ as structural Verilog: 1 circuit, main circuit main
module main (
  input  in_1,
  input  in_2,
  input  in_3,
  output out_4,
  output out_5,
  output out_6,
  output out_7
);

  wire and_1_out, and_2_out, and_3_out, not_1_out;

  not not_1 (not_1_out, in_3);
  and and_1 (and_1_out, not_1_out, in_3);
  and and_2 (and_2_out, in_1, and_1_out);
  and and_3 (and_3_out, and_1_out, in_2);
  S_R_Flip_Flop s_r_ff_1 (.S(and_2_out), .R(and_3_out), .Q(out_5), .Qn(out_6));  // open: clk, preset, reset, en

  assign out_4 = in_1;
  assign out_7 = in_2;
endmodule
