// Logisim project kodersoprioritet.circ as structural Verilog: 1 circuit, main circuit main
module main (
  input  in_1,
  input  in_2,
  input  in_3,
  input  in_4,
  output out_5,
  output out_6,
  output out_7
);

  wire and_2_out, not_1_out, not_2_out, not_3_out, not_4_out;

  not not_1 (not_1_out, in_1);
  not not_2 (not_2_out, in_2);
  not not_3 (not_3_out, in_3);
  not not_4 (not_4_out, in_4);
  and and_1 (out_5, not_1_out, not_2_out, not_4_out, not_3_out);
  and and_2 (and_2_out, in_2, not_4_out);
  or or_1 (out_6, and_2_out, not_4_out);
  or or_2 (out_7, not_3_out, not_4_out);
endmodule
