// Logisim project komparator.circ as structural Verilog: 1 circuit, main circuit main
module main (
  input  in_1,
  input  in_2,
  input  in_3,
  input  in_4,
  input  in_5,
  output out_6,
  output out_7,
  output out_8
);

  wire and_1_out, and_2_out, and_3_out, and_4_out, and_5_out, and_7_out, not_1_out, not_2_out, or_1_out;

  not not_1 (not_1_out, in_1);
  not not_2 (not_2_out, in_2);
  and and_1 (and_1_out, not_1_out, not_2_out);
  and and_2 (and_2_out, in_1, in_2);
  and and_3 (and_3_out, not_1_out, in_2);
  and and_4 (and_4_out, in_1, not_2_out);
  or or_1 (or_1_out, and_1_out, and_2_out);
  and and_5 (and_5_out, and_4_out, in_4);
  and and_6 (out_7, or_1_out, in_4);
  and and_7 (and_7_out, and_3_out, in_4);
  or or_2 (out_6, in_3, and_5_out);
  or or_3 (out_8, and_7_out, in_5);
endmodule
