// Logisim project komparator2bita.circ as structural Verilog: 1 circuit, main circuit main
module main (
  input  in_1,
  input  in_2,
  output out_3,
  output out_4,
  output out_5
);

  wire not_1_out, not_2_out, or_1_out;

  not not_1 (not_1_out, in_1);
  not not_2 (not_2_out, in_2);
  and and_1 (out_3, not_1_out, in_2);
  and and_2 (out_5, in_1, not_2_out);
  or or_1 (or_1_out, out_3, out_5);
  not not_3 (out_4, or_1_out);
endmodule
