// Logisim project parity check.circ as structural Verilog: 1 circuit, main circuit main
module main (
  input  in_1,
  input  in_2,
  input  in_3,
  input  in_4,
  input  in_5,
  output out_6
);

  wire not_1_out, xor_1_out, xor_2_out, xor_3_out;

  xor xor_1 (xor_1_out, in_1, in_2);
  xor xor_2 (xor_2_out, in_3, in_4);
  xor xor_3 (xor_3_out, xor_1_out, xor_2_out);
  not not_1 (not_1_out, xor_3_out);
  xor xor_4 (out_6, not_1_out, in_5);
endmodule
