// Logisim project register11.circ as structural Verilog: 1 circuit, main circuit main
module main (
  input  in_1,
  input  in_2,
  input  in_3,
  input  in_4,
  input  in_5,
  input  in_6,
  input  in_7,
  output out_8
);

  wire and_1_out, and_3_out, and_5_out, and_6_out, s_r_ff_1_q, s_r_ff_2_q, s_r_ff_3_q, s_r_ff_4_q;

  and and_1 (and_1_out, in_1, in_5);
  S_R_Flip_Flop s_r_ff_1 (.S(and_1_out), .R(in_6), .Q(s_r_ff_1_q));  // open: clk, Qn, preset, reset, en
  // AND_Gate and_2 has open pins: in0=s_r_ff_1_q, in1=in_7, out=open
  and and_3 (and_3_out, in_2, in_5);
  S_R_Flip_Flop s_r_ff_2 (.S(and_3_out), .R(in_6), .Q(s_r_ff_2_q));  // open: clk, Qn, preset, reset, en
  // AND_Gate and_4 has open pins: in0=s_r_ff_2_q, in1=in_7, out=open
  and and_5 (and_5_out, in_3, in_5);
  S_R_Flip_Flop s_r_ff_3 (.S(and_5_out), .R(in_6), .Q(s_r_ff_3_q));  // open: clk, Qn, preset, reset, en
  and and_6 (and_6_out, in_4, in_5);
  // AND_Gate and_7 has open pins: in0=s_r_ff_3_q, in1=in_7, out=open
  S_R_Flip_Flop s_r_ff_4 (.S(and_6_out), .R(in_6), .Q(s_r_ff_4_q));  // open: clk, Qn, preset, reset, en
  and and_8 (out_8, s_r_ff_4_q, in_7);
endmodule
