// Logisim project register13.circ as structural Verilog: 1 circuit, main circuit main
module main (
  input  in_1,
  input  in_2,
  input  in_3,
  input  in_4,
  input  in_5,
  output out_6
);

  wire j_k_ff_1_q, j_k_ff_1_qn, j_k_ff_2_q, j_k_ff_2_qn, j_k_ff_3_q, j_k_ff_3_qn, not_1_out;

  J_K_Flip_Flop j_k_ff_1 (
    .J(in_1), .clk(in_3), .K(not_1_out), .Q(j_k_ff_1_q), .Qn(j_k_ff_1_qn), .preset(in_4), .en(in_2),
    .reset(in_5));
  not not_1 (not_1_out, in_1);
  J_K_Flip_Flop j_k_ff_2 (
    .J(j_k_ff_1_q), .clk(in_3), .K(j_k_ff_1_qn), .Q(j_k_ff_2_q), .Qn(j_k_ff_2_qn), .preset(in_4), .en(in_2),
    .reset(in_5));
  J_K_Flip_Flop j_k_ff_3 (
    .J(j_k_ff_2_q), .clk(in_3), .K(j_k_ff_2_qn), .Q(j_k_ff_3_q), .Qn(j_k_ff_3_qn), .preset(in_4), .en(in_2),
    .reset(in_5));
  J_K_Flip_Flop j_k_ff_4 (
    .J(j_k_ff_3_q), .clk(in_3), .K(j_k_ff_3_qn), .Q(out_6), .preset(in_4), .en(in_2), .reset(in_5));  // open: Qn
endmodule
