# Fritzing sketch piano (saved by Fritzing 0.9.3b)
breadboards: 1

parts:
  LED1 = LED - 5mm [color="Red (633nm)" package="5 mm [THT]"]
  LED2 = LED - 5mm [color="Red (633nm)" package="5 mm [THT]"]
  LED3 = LED - 5mm [color="Red (633nm)" package="5 mm [THT]"]
  LED4 = LED - 5mm [color="Red (633nm)" package="5 mm [THT]"]
  LED5 = LED - 5mm [color="Red (633nm)" package="5 mm [THT]"]
  LED6 = LED - 5mm [color="Red (633nm)" package="5 mm [THT]"]
  LED7 = LED - 5mm [color="Red (633nm)" package="5 mm [THT]"]
  LED8 = LED - 5mm [color="Red (633nm)" package="5 mm [THT]"]
  LED9 = LED - 5mm [color="Red (633nm)" package="5 mm [THT]"]
  LED10 = LED - 5mm [color="Red (633nm)" package="5 mm [THT]"]
  LED11 = LED - 5mm [color="Red (633nm)" package="5 mm [THT]"]
  LED12 = LED - 5mm [color="Red (633nm)" package="5 mm [THT]"]
  LED13 = LED - 5mm [color="Red (633nm)" package="5 mm [THT]"]
  LED14 = LED - 5mm [color="Red (633nm)" package="5 mm [THT]"]
  LED15 = LED - 5mm [color="Red (633nm)" package="5 mm [THT]"]
  LED16 = LED - 5mm [color="Red (633nm)" package="5 mm [THT]"]
  R1 = Resistor [tolerance=±5% resistance=220 package=THT]
  R2 = Resistor [tolerance=±5% resistance=220 package=THT]
  R3 = Resistor [tolerance=±5% resistance=220 package=THT]
  R4 = Resistor [tolerance=±5% resistance=220 package=THT]
  R5 = Resistor [tolerance=±5% resistance=220 package=THT]
  R6 = Resistor [tolerance=±5% resistance=220 package=THT]
  R7 = Resistor [tolerance=±5% resistance=220 package=THT]
  R8 = Resistor [tolerance=±5% resistance=220 package=THT]
  R9 = Resistor [tolerance=±5% resistance=220 package=THT]
  R10 = Resistor [tolerance=±5% resistance=220 package=THT]
  R11 = Resistor [tolerance=±5% resistance=220 package=THT]
  R12 = Resistor [tolerance=±5% resistance=220 package=THT]
  R13 = Resistor [tolerance=±5% resistance=220 package=THT]
  R14 = Resistor [tolerance=±5% resistance=220 package=THT]
  R15 = Resistor [tolerance=±5% resistance=220 package=THT]
  R16 = Resistor [tolerance=±5% resistance=220 package=THT]
  Part1 = Arduino Mega 2560 (Rev3)
  U1 = BUTTONPAD-4X4 [package=buttonpad-4x4-special]
  J1 = Piezo Speaker

nets:
  N1: LED1.anode, R16.Pin_1, Part1.D22
  N2: LED2.anode, R15.Pin_1, Part1.D23
  N3: LED3.anode, R14.Pin_1, Part1.D24
  N4: LED4.anode, R13.Pin_1, Part1.D25
  N5: LED5.anode, R12.Pin_1, Part1.D26
  N6: LED6.anode, R11.Pin_1, Part1.D27
  N7: LED7.anode, R10.Pin_1, Part1.D28
  N8: LED8.anode, R9.Pin_1, Part1.D29
  N9: LED9.anode, R8.Pin_1, Part1.D30
  N10: LED10.anode, LED12.anode, R5.Pin_1, R7.Pin_1, Part1.D31
  N11: LED11.anode, R6.Pin_1, Part1.D32
  N12: LED13.anode, R4.Pin_1, Part1.D34
  N13: LED14.anode, R3.Pin_1, Part1.D33
  N14: LED15.anode, R2.Pin_1, Part1.D36
  N15: LED16.anode, R1.Pin_1, Part1.D35
  N16: Part1.GND, J1.pin1
  N17: Part1.D12_PWM, J1.pin2
  N18: Part1.D9_PWM, U1.G$4_RED
  N19: Part1.D8_PWM, U1.G$5_RED
  N20: Part1.D2_PWM, U1.G$5_GRN
  N21: Part1.D3_PWM, U1.G$6_BLU
  N22: Part1.D4_PWM, U1.G$3_SIG1
  N23: Part1.D5_PWM, U1.G$2_SIG2
  N24: Part1.D6_PWM, U1.G$5_GND
  N25: Part1.D7_PWM, U1.G$6_GRN
